// Digital circuit 16bit-16-to-1-MUX.dig as structural Verilog
module _16bit_16_to_1_MUX (
  input  [15:0] D0,
  input  [15:0] D1,
  input  [15:0] D2,
  input  [15:0] D3,
  input  [15:0] D4,
  input  [15:0] D5,
  input  [15:0] D6,
  input  [15:0] D7,
  input  [15:0] D8,
  input  [15:0] D9,
  input  [15:0] D10,
  input  [15:0] D11,
  input  [15:0] D12,
  input  [15:0] D13,
  input  [15:0] D14,
  input  [15:0] D15,
  input  [3:0] S,
  output [15:0] Y
);

  wire [15:0] HIGH_ot, LOW_ot;

  _16bit_8_to_1_MUX LOW (
    .OP(S[2:0]), .AD(D0), .SB(D1), .ND(D2), .OR(D3), .XR(D4), .NT(D5), .SP(D6), .SP2(D7), .OT(LOW_ot));
  _16bit_8_to_1_MUX HIGH (
    .OP(S[2:0]), .AD(D8), .SB(D9), .ND(D10), .OR(D11), .XR(D12), .NT(D13), .SP(D14), .SP2(D15), .OT(HIGH_ot));
  _16bit2_to_1MUX _16bit2_to_1mux_1 (.A(LOW_ot), .B(HIGH_ot), .S(S[3]), .O(Y));
endmodule
