// Digital circuit 16bit-8-to-1-MUX.dig as structural Verilog
module _16bit_8_to_1_MUX (
  input  [2:0] OP,
  input  [15:0] AD,
  input  [15:0] SB,
  input  [15:0] ND,
  input  [15:0] OR,
  input  [15:0] XR,
  input  [15:0] NT,
  input  [15:0] SP,
  input  [15:0] SP2,
  output [15:0] OT
);

  _8_to_1_MUX _8_to_1_mux_1 (.S(OP), .Input({SP2[0], SP[0], NT[0], XR[0], OR[0], ND[0], SB[0], AD[0]}), .OUT(OT[0]));
  _8_to_1_MUX _8_to_1_mux_2 (.S(OP), .Input({SP2[1], SP[1], NT[1], XR[1], OR[1], ND[1], SB[1], AD[1]}), .OUT(OT[1]));
  _8_to_1_MUX _8_to_1_mux_3 (.S(OP), .Input({SP2[2], SP[2], NT[2], XR[2], OR[2], ND[2], SB[2], AD[2]}), .OUT(OT[2]));
  _8_to_1_MUX _8_to_1_mux_4 (.S(OP), .Input({SP2[3], SP[3], NT[3], XR[3], OR[3], ND[3], SB[3], AD[3]}), .OUT(OT[3]));
  _8_to_1_MUX _8_to_1_mux_5 (.S(OP), .Input({SP2[4], SP[4], NT[4], XR[4], OR[4], ND[4], SB[4], AD[4]}), .OUT(OT[4]));
  _8_to_1_MUX _8_to_1_mux_6 (.S(OP), .Input({SP2[5], SP[5], NT[5], XR[5], OR[5], ND[5], SB[5], AD[5]}), .OUT(OT[5]));
  _8_to_1_MUX _8_to_1_mux_7 (.S(OP), .Input({SP2[6], SP[6], NT[6], XR[6], OR[6], ND[6], SB[6], AD[6]}), .OUT(OT[6]));
  _8_to_1_MUX _8_to_1_mux_8 (.S(OP), .Input({SP2[7], SP[7], NT[7], XR[7], OR[7], ND[7], SB[7], AD[7]}), .OUT(OT[7]));
  _8_to_1_MUX _8_to_1_mux_9 (.S(OP), .Input({SP2[8], SP[8], NT[8], XR[8], OR[8], ND[8], SB[8], AD[8]}), .OUT(OT[8]));
  _8_to_1_MUX _8_to_1_mux_10 (.S(OP), .Input({SP2[9], SP[9], NT[9], XR[9], OR[9], ND[9], SB[9], AD[9]}), .OUT(OT[9]));
  _8_to_1_MUX _8_to_1_mux_11 (
    .S(OP), .Input({SP2[10], SP[10], NT[10], XR[10], OR[10], ND[10], SB[10], AD[10]}), .OUT(OT[10]));
  _8_to_1_MUX _8_to_1_mux_12 (
    .S(OP), .Input({SP2[11], SP[11], NT[11], XR[11], OR[11], ND[11], SB[11], AD[11]}), .OUT(OT[11]));
  _8_to_1_MUX _8_to_1_mux_13 (
    .S(OP), .Input({SP2[12], SP[12], NT[12], XR[12], OR[12], ND[12], SB[12], AD[12]}), .OUT(OT[12]));
  _8_to_1_MUX _8_to_1_mux_14 (
    .S(OP), .Input({SP2[13], SP[13], NT[13], XR[13], OR[13], ND[13], SB[13], AD[13]}), .OUT(OT[13]));
  _8_to_1_MUX _8_to_1_mux_15 (
    .S(OP), .Input({SP2[14], SP[14], NT[14], XR[14], OR[14], ND[14], SB[14], AD[14]}), .OUT(OT[14]));
  _8_to_1_MUX _8_to_1_mux_16 (
    .S(OP), .Input({SP2[15], SP[15], NT[15], XR[15], OR[15], ND[15], SB[15], AD[15]}), .OUT(OT[15]));
endmodule
