// Digital circuit 16bit2-to-1MUX.dig as structural Verilog
module _16bit2_to_1MUX (
  input  [15:0] A,
  input  [15:0] B,
  input  S,
  output [15:0] O
);

  wire [15:0] and16_1_o, and16_2_o, not16_1_o;

  NOT16 not16_1 (.A({16{S}}), .O(not16_1_o));
  AND16 and16_1 (.A(A), .B(not16_1_o), .O(and16_1_o));
  AND16 and16_2 (.A({16{S}}), .B(B), .O(and16_2_o));
  OR16 or16_1 (.A(and16_1_o), .B(and16_2_o), .O(O));
endmodule
