// Digital circuit 2-to-1-MUX.dig as structural Verilog
module _2_to_1_MUX (
  input  A,
  input  B,
  input  S,
  output O
);

  wire and_1_o, and_2_o, not_1_o;

  NOT not_1 (.A(S), .O(not_1_o));
  AND and_1 (.A(A), .B(not_1_o), .O(and_1_o));
  AND and_2 (.A(S), .B(B), .O(and_2_o));
  OR or_1 (.A(and_1_o), .B(and_2_o), .O(O));
endmodule
