// Digital circuit 3-to-8-decoder.dig as structural Verilog
module _3_to_8_decoder (
  input  [2:0] chs,
  input  W,
  output _000,
  output _001,
  output _010,
  output _011,
  output _100,
  output _101,
  output _110,
  output _111
);

  wire and_1_o, and_2_o, and_3_o, and_4_o, and_5_o, and_6_o, and_7_o, and_8_o, and_9_o, and_10_o, and_11_o,
       and_12_o, and_13_o, and_14_o, and_15_o, and_16_o, not_1_o, not_2_o, not_3_o, not_4_o, not_5_o,
       not_6_o, not_7_o, not_8_o, not_9_o, not_10_o, not_11_o, not_12_o;

  NOT not_1 (.A(chs[0]), .O(not_1_o));
  NOT not_2 (.A(chs[1]), .O(not_2_o));
  NOT not_3 (.A(chs[2]), .O(not_3_o));
  NOT not_4 (.A(chs[1]), .O(not_4_o));
  NOT not_5 (.A(chs[2]), .O(not_5_o));
  NOT not_6 (.A(chs[0]), .O(not_6_o));
  NOT not_7 (.A(chs[2]), .O(not_7_o));
  NOT not_8 (.A(chs[2]), .O(not_8_o));
  NOT not_9 (.A(chs[0]), .O(not_9_o));
  NOT not_10 (.A(chs[1]), .O(not_10_o));
  NOT not_11 (.A(chs[1]), .O(not_11_o));
  NOT not_12 (.A(chs[0]), .O(not_12_o));
  AND and_1 (.A(not_1_o), .B(not_3_o), .O(and_1_o));
  AND and_2 (.A(chs[0]), .B(not_5_o), .O(and_2_o));
  AND and_3 (.A(not_6_o), .B(not_7_o), .O(and_3_o));
  AND and_4 (.A(chs[0]), .B(not_8_o), .O(and_4_o));
  AND and_5 (.A(not_9_o), .B(chs[2]), .O(and_5_o));
  AND and_6 (.A(chs[0]), .B(chs[2]), .O(and_6_o));
  AND and_7 (.A(not_12_o), .B(chs[2]), .O(and_7_o));
  AND and_8 (.A(chs[0]), .B(chs[2]), .O(and_8_o));
  AND and_9 (.A(and_1_o), .B(not_2_o), .O(and_9_o));
  AND and_10 (.A(and_2_o), .B(not_4_o), .O(and_10_o));
  AND and_11 (.A(and_3_o), .B(chs[1]), .O(and_11_o));
  AND and_12 (.A(and_4_o), .B(chs[1]), .O(and_12_o));
  AND and_13 (.A(and_5_o), .B(not_10_o), .O(and_13_o));
  AND and_14 (.A(and_6_o), .B(not_11_o), .O(and_14_o));
  AND and_15 (.A(and_7_o), .B(chs[1]), .O(and_15_o));
  AND and_16 (.A(and_8_o), .B(chs[1]), .O(and_16_o));
  AND and_17 (.A(and_9_o), .B(W), .O(_000));
  AND and_18 (.A(and_10_o), .B(W), .O(_001));
  AND and_19 (.A(and_11_o), .B(W), .O(_010));
  AND and_20 (.A(and_12_o), .B(W), .O(_011));
  AND and_21 (.A(and_13_o), .B(W), .O(_100));
  AND and_22 (.A(and_14_o), .B(W), .O(_101));
  AND and_23 (.A(and_15_o), .B(W), .O(_110));
  AND and_24 (.A(and_16_o), .B(W), .O(_111));
endmodule
