// Digital circuit 4-to-1-MUX.dig as structural Verilog
module _4_to_1_MUX (
  input  S1,
  input  S2,
  input  A1,
  input  B1,
  input  A2,
  input  B2,
  output O
);

  wire _2_to_1_mux_1_o, _2_to_1_mux_2_o;

  _2_to_1_MUX _2_to_1_mux_1 (.A(A1), .B(B1), .S(S1), .O(_2_to_1_mux_1_o));
  _2_to_1_MUX _2_to_1_mux_2 (.A(A2), .B(B2), .S(S1), .O(_2_to_1_mux_2_o));
  _2_to_1_MUX _2_to_1_mux_3 (.A(_2_to_1_mux_1_o), .B(_2_to_1_mux_2_o), .S(S2), .O(O));
endmodule
