// Digital circuit 4-to-16-decoder.dig as structural Verilog
module _4_to_16_decoder (
  input  [3:0] sel,
  input  W,
  output [15:0] OUT
);

  wire and_1_o, and_2_o, not_1_o;

  NOT not_1 (.A(sel[3]), .O(not_1_o));
  AND and_1 (.A(W), .B(sel[3]), .O(and_1_o));
  AND and_2 (.A(W), .B(not_1_o), .O(and_2_o));
  _3_to_8_decoder LOW (
    .chs(sel[2:0]), .W(and_2_o), ._000(OUT[0]), ._001(OUT[1]), ._010(OUT[2]), ._011(OUT[3]), ._100(OUT[4]),
    ._101(OUT[5]), ._110(OUT[6]), ._111(OUT[7]));
  _3_to_8_decoder HIGH (
    .chs(sel[2:0]), .W(and_1_o), ._000(OUT[8]), ._001(OUT[9]), ._010(OUT[10]), ._011(OUT[11]),
    ._100(OUT[12]), ._101(OUT[13]), ._110(OUT[14]), ._111(OUT[15]));
endmodule
