// Digital circuit 8-to-1-MUX.dig as structural Verilog
module _8_to_1_MUX (
  input  [2:0] S,
  input  [7:0] Input,
  output OUT
);

  wire _4_to_1_mux_1_o, _4_to_1_mux_2_o;

  _4_to_1_MUX _4_to_1_mux_1 (
    .S1(S[0]), .S2(S[1]), .A1(Input[0]), .B1(Input[1]), .A2(Input[2]), .B2(Input[3]), .O(_4_to_1_mux_1_o));
  _4_to_1_MUX _4_to_1_mux_2 (
    .S1(S[0]), .S2(S[1]), .A1(Input[4]), .B1(Input[5]), .A2(Input[6]), .B2(Input[7]), .O(_4_to_1_mux_2_o));
  _2_to_1_MUX _2_to_1_mux_1 (.A(_4_to_1_mux_1_o), .B(_4_to_1_mux_2_o), .S(S[2]), .O(OUT));
endmodule
