// Digital circuit ALU.dig as structural Verilog
module ALU (
  input  [2:0] OP,
  input  [15:0] A,
  input  [15:0] B,
  input  Sub,
  output [15:0] O,
  output N,
  output C,
  output V,
  output Z
);

  wire [15:0] and16_1_o, full_add_sub_1_s, not16_1_o, or16_1_o, xor16_1_o;

  Full_add_sub full_add_sub_1 (.Cin(Sub), .A(A), .B(B), .S(full_add_sub_1_s), .N(N), .C(C), .V(V), .Z(Z));
  AND16 and16_1 (.A(A), .B(B), .O(and16_1_o));
  OR16 or16_1 (.A(A), .B(B), .O(or16_1_o));
  XOR16 xor16_1 (.A(A), .B(B), .O(xor16_1_o));
  NOT16 not16_1 (.A(A), .O(not16_1_o));
  _16bit_8_to_1_MUX _16bit_8_to_1_mux_1 (
    .OP(OP), .AD({16{1'b0}}), .SB(full_add_sub_1_s), .ND(and16_1_o), .OR(or16_1_o), .XR(xor16_1_o),
    .NT(not16_1_o), .SP({16{1'b0}}), .SP2({16{1'b0}}), .OT(O));
endmodule
