// Digital circuit AND.dig as structural Verilog
module AND (
  input  A,
  input  B,
  output O
);

  wire nand_1_o, nand_2_o;

  NAND nand_1 (.A(A), .B(B), .O(nand_1_o));
  NAND nand_2 (.A(B), .B(A), .O(nand_2_o));
  NAND nand_3 (.A(nand_1_o), .B(nand_2_o), .O(O));
endmodule
