// Digital circuit CPU.dig as structural Verilog
module CPU (
  input  R,
  input  clock
);

  wire alu_1_c, alu_1_n, alu_1_v, alu_1_z, and_1_o, and_2_o, d_ff_1_nq, d_ff_2_q, flags_1_nf, flags_1_vf,
       flags_1_zf, instruction_reader_1_p4, instruction_reader_1_p5, not_1_o, or_1_o;
  wire [1:0] control_1_out_2;
  wire [3:0] instruction_reader_1_p10, instruction_reader_1_p11, instruction_reader_1_p12,
       instruction_reader_1_p13, multiplexer_1_out;
  wire [7:0] instruction_reader_1_p3;
  wire [12:0] control_1_out;
  wire [15:0] alu_1_o, immediate_1_imm, immediate_1_lui, instruction_reader_1_p9, instruction_reader_1_p14,
       ramdualaccess_1_d1, registerfile_1_db, writeback_1_wbdata;
  wire [15:8] instruction_reader_1_p3_2;

  NOT not_1 (.A(clock), .O(not_1_o));
  D_FF d_ff_1 (.D(d_ff_2_q), .C(not_1_o), .nQ(d_ff_1_nq));  // open: Q
  D_FF d_ff_2 (.D(1'b1), .C(clock), .Q(d_ff_2_q));  // open: nQ
  OR or_1 (.A(d_ff_1_nq), .B(R), .O(or_1_o));
  AND and_1 (.A(control_1_out_2[0]), .B(control_1_out_2[1]), .O(and_1_o));
  // Instruction_reader instruction_reader_1: pin names not known; wires that end beside it: or_1_o, clock, {instruction_reader_1_p3_2, instruction_reader_1_p3}, instruction_reader_1_p4, instruction_reader_1_p5, 1'b0, 1'b0, 1'b0, instruction_reader_1_p9, instruction_reader_1_p10, instruction_reader_1_p11, instruction_reader_1_p12, instruction_reader_1_p13, instruction_reader_1_p14
  Multiplexer #(.Bits(4)) multiplexer_1 (
    .sel(and_1_o), .in_0(instruction_reader_1_p11), .in_1(instruction_reader_1_p13), .out(multiplexer_1_out));
  NOT not_2 (.A(control_1_out[12]), .O(instruction_reader_1_p5));
  immediate immediate_1 (
    .RA(instruction_reader_1_p11), .RB(instruction_reader_1_p12),
    .RDval({instruction_reader_1_p3_2, instruction_reader_1_p3}), .IMM(immediate_1_imm), .LUI(immediate_1_lui));
  RegisterFile #(.AddrBits(4), .Bits(16)) registerfile_1 (
    .Din(writeback_1_wbdata), .we(control_1_out[0]), .Rw(instruction_reader_1_p13), .C(clock),
    .Ra(multiplexer_1_out), .Rb(instruction_reader_1_p12),
    .Da({instruction_reader_1_p3_2, instruction_reader_1_p3}), .Db(registerfile_1_db));
  writeback writeback_1 (
    .ALU(alu_1_o), .MEM(ramdualaccess_1_d1), .IMM(immediate_1_imm), .LUI(immediate_1_lui),
    .WBsrc(control_1_out_2), .WBdata(writeback_1_wbdata));
  control control_1 (.OP(instruction_reader_1_p10), .OUT({control_1_out[12:7], control_1_out_2, control_1_out[4:0]}));
  ALU alu_1 (
    .OP(control_1_out[3:1]), .A({instruction_reader_1_p3_2, instruction_reader_1_p3}), .B(registerfile_1_db),
    .Sub(control_1_out[4]), .O(alu_1_o), .N(alu_1_n), .C(alu_1_c), .V(alu_1_v), .Z(alu_1_z));
  flags flags_1 (
    .N(alu_1_n), .C(alu_1_c), .V(alu_1_v), .Z(alu_1_z), .FlagWrite(control_1_out[11]), .CLK(clock),
    .Zf(flags_1_zf), .Nf(flags_1_nf), .Vf(flags_1_vf));  // open: Cf
  RAMDualAccess #(.AddrBits(16), .isProgramMemory("true"), .Bits(16)) ramdualaccess_1 (
    .str(control_1_out[7]), .C(clock), .ld(1'b1), .A1({instruction_reader_1_p3_2, instruction_reader_1_p3}),
    .Din1(registerfile_1_db), .A2(instruction_reader_1_p14), .D1(ramdualaccess_1_d1),
    .D2(instruction_reader_1_p9));
  branch branch_1 (
    .Cond(control_1_out[10:9]), .Zf(flags_1_zf), .Nf(flags_1_nf), .Vf(flags_1_vf), .Branch(control_1_out[8]),
    .JumpEn(instruction_reader_1_p4));
  AND and_2 (.A(control_1_out[7]), .B(instruction_reader_1_p3_2[15]), .O(and_2_o));
  GraphicCard #(.graphicHeight(10), .graphicWidth(10), .Bits(16)) VRAM (
    .A(instruction_reader_1_p3), .str(and_2_o), .C(clock), .ld(1'b0), .B(1'b0), .D(registerfile_1_db));

  // Notes on the sheet:
  //   clock: Hz: 50
endmodule
