// Digital circuit D-latch.dig as structural Verilog
module D_latch (
  input  D,
  input  CLK,
  input  R,
  output O
);

  wire and_1_o, and_2_o, nor_1_o, nor_2_o, not_1_o;

  AND and_1 (.A(D), .B(CLK), .O(and_1_o));
  NOT not_1 (.A(D), .O(not_1_o));
  AND and_2 (.A(not_1_o), .B(CLK), .O(and_2_o));
  NOR nor_1 (.A(and_1_o), .B(nor_2_o), .O(nor_1_o));
  NOR nor_2 (.A(O), .B(and_2_o), .O(nor_2_o));
  OR or_1 (.A(R), .B(nor_1_o), .O(O));
endmodule
