// Digital circuit Full-add-sub.dig as structural Verilog
module Full_add_sub (
  input  Cin,
  input  [15:0] A,
  input  [15:0] B,
  output [15:0] S,
  output N,
  output C,
  output V,
  output Z
);

  wire or_1_o, or_2_o, or_3_o, or_4_o, or_5_o, or_6_o, or_7_o, or_8_o, or_9_o, or_10_o, or_11_o, or_12_o,
       or_13_o, or_14_o, or_15_o, parallel_adder_1_c4, parallel_adder_2_c4, parallel_adder_3_c4,
       parallel_adder_4_c3, xor_1_o, xor_2_o, xor_3_o, xor_4_o, xor_5_o, xor_6_o, xor_7_o, xor_8_o, xor_9_o,
       xor_10_o, xor_11_o, xor_12_o, xor_13_o, xor_14_o, xor_15_o, xor_16_o;

  XOR xor_1 (.A(B[0]), .B(Cin), .O(xor_1_o));
  XOR xor_2 (.A(B[1]), .B(Cin), .O(xor_2_o));
  XOR xor_3 (.A(B[2]), .B(Cin), .O(xor_3_o));
  XOR xor_4 (.A(B[3]), .B(Cin), .O(xor_4_o));
  XOR xor_5 (.A(B[4]), .B(Cin), .O(xor_5_o));
  XOR xor_6 (.A(B[5]), .B(Cin), .O(xor_6_o));
  XOR xor_7 (.A(B[6]), .B(Cin), .O(xor_7_o));
  XOR xor_8 (.A(B[7]), .B(Cin), .O(xor_8_o));
  XOR xor_9 (.A(B[8]), .B(Cin), .O(xor_9_o));
  XOR xor_10 (.A(B[9]), .B(Cin), .O(xor_10_o));
  XOR xor_11 (.A(B[10]), .B(Cin), .O(xor_11_o));
  XOR xor_12 (.A(B[11]), .B(Cin), .O(xor_12_o));
  XOR xor_13 (.A(B[12]), .B(Cin), .O(xor_13_o));
  XOR xor_14 (.A(B[13]), .B(Cin), .O(xor_14_o));
  XOR xor_15 (.A(B[14]), .B(Cin), .O(xor_15_o));
  XOR xor_16 (.A(B[15]), .B(Cin), .O(xor_16_o));
  Parallel_adder parallel_adder_1 (
    .A0(A[0]), .A1(A[1]), .A2(A[2]), .A3(A[3]), .B0(xor_1_o), .B1(xor_2_o), .B2(xor_3_o), .B3(xor_4_o),
    .Cin(Cin), .S0(S[0]), .S1(S[1]), .S2(S[2]), .S3(S[3]), .C4(parallel_adder_1_c4));  // open: C3
  Parallel_adder parallel_adder_2 (
    .A0(A[8]), .A1(A[9]), .A2(A[10]), .A3(A[11]), .B0(xor_9_o), .B1(xor_10_o), .B2(xor_11_o), .B3(xor_12_o),
    .Cin(parallel_adder_3_c4), .S0(S[8]), .S1(S[9]), .S2(S[10]), .S3(S[11]), .C4(parallel_adder_2_c4));  // open: C3
  Parallel_adder parallel_adder_3 (
    .A0(A[4]), .A1(A[5]), .A2(A[6]), .A3(A[7]), .B0(xor_5_o), .B1(xor_6_o), .B2(xor_7_o), .B3(xor_8_o),
    .Cin(parallel_adder_1_c4), .S0(S[4]), .S1(S[5]), .S2(S[6]), .S3(S[7]), .C4(parallel_adder_3_c4));  // open: C3
  Parallel_adder parallel_adder_4 (
    .A0(A[12]), .A1(A[13]), .A2(A[14]), .A3(A[15]), .B0(xor_13_o), .B1(xor_14_o), .B2(xor_15_o),
    .B3(xor_16_o), .Cin(parallel_adder_2_c4), .S0(S[12]), .S1(S[13]), .S2(S[14]), .S3(N), .C4(C),
    .C3(parallel_adder_4_c3));
  XOR xor_17 (.A(C), .B(parallel_adder_4_c3), .O(V));
  OR or_1 (.A(S[0]), .B(S[1]), .O(or_1_o));
  OR or_2 (.A(S[2]), .B(S[3]), .O(or_2_o));
  OR or_3 (.A(S[4]), .B(S[5]), .O(or_3_o));
  OR or_4 (.A(S[6]), .B(S[7]), .O(or_4_o));
  OR or_5 (.A(S[8]), .B(S[9]), .O(or_5_o));
  OR or_6 (.A(S[10]), .B(S[11]), .O(or_6_o));
  OR or_7 (.A(S[12]), .B(S[13]), .O(or_7_o));
  OR or_8 (.A(S[14]), .B(N), .O(or_8_o));
  OR or_9 (.A(or_1_o), .B(or_2_o), .O(or_9_o));
  OR or_10 (.A(or_3_o), .B(or_4_o), .O(or_10_o));
  OR or_11 (.A(or_5_o), .B(or_6_o), .O(or_11_o));
  OR or_12 (.A(or_7_o), .B(or_8_o), .O(or_12_o));
  OR or_13 (.A(or_9_o), .B(or_10_o), .O(or_13_o));
  OR or_14 (.A(or_11_o), .B(or_12_o), .O(or_14_o));
  OR or_15 (.A(or_13_o), .B(or_14_o), .O(or_15_o));
  NOT not_1 (.A(or_15_o), .O(Z));

  assign S[15] = N;
endmodule
