// Digital circuit Incrementer.dig as structural Verilog
module Incrementer (
  input  [15:0] A,
  input  Cin,
  output [15:0] S
);

  wire and_1_o, and_2_o, and_3_o, and_4_o, and_5_o, and_6_o, and_7_o, and_8_o, and_9_o, and_10_o, and_11_o,
       and_13_o, and_14_o, and_15_o, and_16_o;

  AND and_1 (.A(A[0]), .B(Cin), .O(and_1_o));
  AND and_2 (.A(and_1_o), .B(A[1]), .O(and_2_o));
  AND and_3 (.A(and_16_o), .B(A[10]), .O(and_3_o));
  AND and_4 (.A(and_2_o), .B(A[2]), .O(and_4_o));
  XOR xor_1 (.A(A[10]), .B(and_16_o), .O(S[10]));
  AND and_5 (.A(and_3_o), .B(A[11]), .O(and_5_o));
  AND and_6 (.A(and_4_o), .B(A[3]), .O(and_6_o));
  XOR xor_2 (.A(A[11]), .B(and_3_o), .O(S[11]));
  AND and_7 (.A(and_5_o), .B(A[12]), .O(and_7_o));
  XOR xor_3 (.A(A[0]), .B(Cin), .O(S[0]));
  XOR xor_4 (.A(A[1]), .B(and_1_o), .O(S[1]));
  XOR xor_5 (.A(A[12]), .B(and_5_o), .O(S[12]));
  AND and_8 (.A(and_7_o), .B(A[13]), .O(and_8_o));
  XOR xor_6 (.A(A[2]), .B(and_2_o), .O(S[2]));
  XOR xor_7 (.A(A[3]), .B(and_4_o), .O(S[3]));
  AND and_9 (.A(and_6_o), .B(A[4]), .O(and_9_o));
  XOR xor_8 (.A(A[13]), .B(and_7_o), .O(S[13]));
  AND and_10 (.A(and_8_o), .B(A[14]), .O(and_10_o));
  XOR xor_9 (.A(A[4]), .B(and_6_o), .O(S[4]));
  AND and_11 (.A(and_9_o), .B(A[5]), .O(and_11_o));
  XOR xor_10 (.A(A[14]), .B(and_8_o), .O(S[14]));
  AND and_12 (.A(and_10_o), .B(A[15]));  // open: O
  XOR xor_11 (.A(A[5]), .B(and_9_o), .O(S[5]));
  AND and_13 (.A(and_11_o), .B(A[6]), .O(and_13_o));
  XOR xor_12 (.A(A[15]), .B(and_10_o), .O(S[15]));
  AND and_14 (.A(and_13_o), .B(A[7]), .O(and_14_o));
  XOR xor_13 (.A(A[6]), .B(and_11_o), .O(S[6]));
  XOR xor_14 (.A(A[7]), .B(and_13_o), .O(S[7]));
  AND and_15 (.A(and_14_o), .B(A[8]), .O(and_15_o));
  XOR xor_15 (.A(A[8]), .B(and_14_o), .O(S[8]));
  AND and_16 (.A(and_15_o), .B(A[9]), .O(and_16_o));
  XOR xor_16 (.A(A[9]), .B(and_15_o), .O(S[9]));
endmodule
