// Digital circuit Instruction reader.dig as structural Verilog
module Instruction_reader (
  input  R,
  input  clk,
  input  [15:0] JMP_ADDR,
  input  JMPE,
  input  WE,
  input  [15:0] Data_in,
  input  STR,
  input  [15:0] STR_ADDR,
  input  [15:0] INSTR_IN,
  output [3:0] OP,
  output [3:0] RA,
  output [3:0] RB,
  output [3:0] RD,
  output [15:0] PC_OUT
);

  Register register_1 (.Value(INSTR_IN), .clk(clk), .WE(WE), .R(R), .SV({OP, RD, RA, RB}));
  Program_Counter program_counter_1 (.JMP(JMP_ADDR), .JE(JMPE), .clk(clk), .R(R), .WE(WE), .O(PC_OUT));

  // Notes on the sheet:
  //   WE: default 1
endmodule
