// Digital circuit NOT16.dig as structural Verilog
module NOT16 (
  input  [15:0] A,
  output [15:0] O
);

  NOT not_1 (.A(A[0]), .O(O[0]));
  NOT not_2 (.A(A[1]), .O(O[1]));
  NOT not_3 (.A(A[2]), .O(O[2]));
  NOT not_4 (.A(A[3]), .O(O[3]));
  NOT not_5 (.A(A[4]), .O(O[4]));
  NOT not_6 (.A(A[5]), .O(O[5]));
  NOT not_7 (.A(A[6]), .O(O[6]));
  NOT not_8 (.A(A[7]), .O(O[7]));
  NOT not_9 (.A(A[8]), .O(O[8]));
  NOT not_10 (.A(A[9]), .O(O[9]));
  NOT not_11 (.A(A[10]), .O(O[10]));
  NOT not_12 (.A(A[11]), .O(O[11]));
  NOT not_13 (.A(A[12]), .O(O[12]));
  NOT not_14 (.A(A[13]), .O(O[13]));
  NOT not_15 (.A(A[14]), .O(O[14]));
  NOT not_16 (.A(A[15]), .O(O[15]));
endmodule
