// Digital circuit OR.dig as structural Verilog
module OR (
  input  A,
  input  B,
  output O
);

  wire not_1_o;

  NOT not_1 (.A(A), .O(not_1_o));
  NOT not_2 (.A(B));  // open: O
  NAND nand_1 (.A(not_1_o));  // open: B, O
endmodule
