// Digital circuit OR16.dig as structural Verilog
module OR16 (
  input  [15:0] A,
  input  [15:0] B,
  output [15:0] O
);

  OR or_1 (.A(A[0]), .B(B[0]), .O(O[0]));
  OR or_2 (.A(A[1]), .B(B[1]), .O(O[1]));
  OR or_3 (.A(A[2]), .B(B[2]), .O(O[2]));
  OR or_4 (.A(A[3]), .B(B[3]), .O(O[3]));
  OR or_5 (.A(A[4]), .B(B[4]), .O(O[4]));
  OR or_6 (.A(A[5]), .B(B[5]), .O(O[5]));
  OR or_7 (.A(A[6]), .B(B[6]), .O(O[6]));
  OR or_8 (.A(A[7]), .B(B[7]), .O(O[7]));
  OR or_9 (.A(A[8]), .B(B[8]), .O(O[8]));
  OR or_10 (.A(A[9]), .B(B[9]), .O(O[9]));
  OR or_11 (.A(A[10]), .B(B[10]), .O(O[10]));
  OR or_12 (.A(A[11]), .B(B[11]), .O(O[11]));
  OR or_13 (.A(A[12]), .B(B[12]), .O(O[12]));
  OR or_14 (.A(A[13]), .B(B[13]), .O(O[13]));
  OR or_15 (.A(A[14]), .B(B[14]), .O(O[14]));
  OR or_16 (.A(A[15]), .B(B[15]), .O(O[15]));
endmodule
