// Digital circuit Parallel adder.dig as structural Verilog
module Parallel_adder (
  input  A0,
  input  A1,
  input  A2,
  input  A3,
  input  B0,
  input  B1,
  input  B2,
  input  B3,
  input  Cin,
  output S0,
  output S1,
  output S2,
  output S3,
  output C4,
  output C3
);

  wire and_1_o, and_2_o, and_3_o, and_4_o, and_5_o, and_6_o, and_7_o, and_8_o, and_9_o, and_10_o, and_11_o,
       and_12_o, and_13_o, and_14_o, and_15_o, and_16_o, and_17_o, and_18_o, and_19_o, and_20_o, and_21_o,
       and_22_o, and_23_o, and_24_o, or_1_o, or_2_o, or_3_o, or_4_o, or_5_o, or_7_o, or_8_o, or_9_o, xor_1_o,
       xor_2_o, xor_3_o, xor_4_o;

  XOR xor_1 (.A(A0), .B(B0), .O(xor_1_o));
  XOR xor_2 (.A(A1), .B(B1), .O(xor_2_o));
  XOR xor_3 (.A(A2), .B(B2), .O(xor_3_o));
  XOR xor_4 (.A(A3), .B(B3), .O(xor_4_o));
  AND and_1 (.A(A0), .B(B0), .O(and_1_o));
  AND and_2 (.A(A1), .B(B1), .O(and_2_o));
  AND and_3 (.A(A2), .B(B2), .O(and_3_o));
  AND and_4 (.A(A3), .B(B3), .O(and_4_o));
  AND and_5 (.A(xor_1_o), .B(Cin), .O(and_5_o));
  AND and_6 (.A(xor_1_o), .B(xor_2_o), .O(and_6_o));
  AND and_7 (.A(xor_3_o), .B(Cin), .O(and_7_o));
  AND and_8 (.A(xor_3_o), .B(xor_2_o), .O(and_8_o));
  AND and_9 (.A(xor_3_o), .B(and_2_o), .O(and_9_o));
  OR or_1 (.A(and_5_o), .B(and_1_o), .O(or_1_o));
  AND and_10 (.A(xor_1_o), .B(xor_2_o), .O(and_10_o));
  AND and_11 (.A(and_6_o), .B(and_7_o), .O(and_11_o));
  AND and_12 (.A(and_8_o), .B(and_1_o), .O(and_12_o));
  AND and_13 (.A(and_1_o), .B(xor_2_o), .O(and_13_o));
  AND and_14 (.A(and_10_o), .B(Cin), .O(and_14_o));
  OR or_2 (.A(and_11_o), .B(and_12_o), .O(or_2_o));
  AND and_15 (.A(xor_1_o), .B(xor_2_o), .O(and_15_o));
  AND and_16 (.A(xor_3_o), .B(xor_4_o), .O(and_16_o));
  AND and_17 (.A(xor_2_o), .B(xor_3_o), .O(and_17_o));
  AND and_18 (.A(xor_4_o), .B(and_1_o), .O(and_18_o));
  AND and_19 (.A(xor_3_o), .B(xor_4_o), .O(and_19_o));
  OR or_3 (.A(and_13_o), .B(and_14_o), .O(or_3_o));
  OR or_4 (.A(or_2_o), .B(and_9_o), .O(or_4_o));
  AND and_20 (.A(and_15_o), .B(and_16_o), .O(and_20_o));
  AND and_21 (.A(and_17_o), .B(and_18_o), .O(and_21_o));
  AND and_22 (.A(and_19_o), .B(and_2_o), .O(and_22_o));
  AND and_23 (.A(and_3_o), .B(xor_4_o), .O(and_23_o));
  OR or_5 (.A(and_2_o), .B(or_3_o), .O(or_5_o));
  OR or_6 (.A(or_4_o), .B(and_3_o), .O(C3));
  AND and_24 (.A(and_20_o), .B(Cin), .O(and_24_o));
  OR or_7 (.A(and_23_o), .B(and_4_o), .O(or_7_o));
  OR or_8 (.A(and_24_o), .B(and_21_o), .O(or_8_o));
  OR or_9 (.A(or_8_o), .B(and_22_o), .O(or_9_o));
  OR or_10 (.A(or_9_o), .B(or_7_o), .O(C4));
  XOR xor_5 (.A(xor_1_o), .B(Cin), .O(S0));
  XOR xor_6 (.A(xor_2_o), .B(or_1_o), .O(S1));
  XOR xor_7 (.A(xor_3_o), .B(or_5_o), .O(S2));
  XOR xor_8 (.A(xor_4_o), .B(C3), .O(S3));

  // Notes on the sheet:
  //   C1
  //   C2
  //   C3
  //   C4
endmodule
