// Digital circuit Program Counter.dig as structural Verilog
module Program_Counter (
  input  [15:0] JMP,
  input  JE,
  input  clk,
  input  R,
  input  WE,
  output [15:0] O
);

  wire [15:0] _16bit2_to_1mux_1_o, incrementer_1_s;

  Incrementer incrementer_1 (.A(O), .Cin(1'b1), .S(incrementer_1_s));
  Register register_1 (.Value(_16bit2_to_1mux_1_o), .clk(clk), .WE(WE), .R(R), .SV(O));
  _16bit2_to_1MUX _16bit2_to_1mux_1 (.A(incrementer_1_s), .B(JMP), .S(JE), .O(_16bit2_to_1mux_1_o));
endmodule
