// Digital circuit Register.dig as structural Verilog
module Register (
  input  [15:0] Value,
  input  clk,
  input  WE,
  input  R,
  output [15:0] SV
);

  wire [7:0] _16bit2_to_1mux_1_o;
  wire [15:8] _16bit2_to_1mux_1_o_2;

  _16bit2_to_1MUX _16bit2_to_1mux_1 (.A(SV), .B(Value), .S(WE), .O({_16bit2_to_1mux_1_o_2, _16bit2_to_1mux_1_o}));
  flip_flop flip_flop_1 (.D(_16bit2_to_1mux_1_o[0]), .CLK(clk), .R(R), .O(SV[0]));
  flip_flop flip_flop_2 (.D(_16bit2_to_1mux_1_o[1]), .CLK(clk), .R(R), .O(SV[1]));
  flip_flop flip_flop_3 (.D(_16bit2_to_1mux_1_o[2]), .CLK(clk), .R(R), .O(SV[2]));
  flip_flop flip_flop_4 (.D(_16bit2_to_1mux_1_o[3]), .CLK(clk), .R(R), .O(SV[3]));
  flip_flop flip_flop_5 (.D(_16bit2_to_1mux_1_o[4]), .CLK(clk), .R(R), .O(SV[4]));
  flip_flop flip_flop_6 (.D(_16bit2_to_1mux_1_o[5]), .CLK(clk), .R(R), .O(SV[5]));
  flip_flop flip_flop_7 (.D(_16bit2_to_1mux_1_o[6]), .CLK(clk), .R(R), .O(SV[6]));
  flip_flop flip_flop_8 (.D(_16bit2_to_1mux_1_o[7]), .CLK(clk), .R(R), .O(SV[7]));
  flip_flop flip_flop_9 (.D(_16bit2_to_1mux_1_o_2[8]), .CLK(clk), .R(R), .O(SV[8]));
  flip_flop flip_flop_10 (.D(_16bit2_to_1mux_1_o_2[9]), .CLK(clk), .R(R), .O(SV[9]));
  flip_flop flip_flop_11 (.D(_16bit2_to_1mux_1_o_2[10]), .CLK(clk), .R(R), .O(SV[10]));
  flip_flop flip_flop_12 (.D(_16bit2_to_1mux_1_o_2[11]), .CLK(clk), .R(R), .O(SV[11]));
  flip_flop flip_flop_13 (.D(_16bit2_to_1mux_1_o_2[12]), .CLK(clk), .R(R), .O(SV[12]));
  flip_flop flip_flop_14 (.D(_16bit2_to_1mux_1_o_2[13]), .CLK(clk), .R(R), .O(SV[13]));
  flip_flop flip_flop_15 (.D(_16bit2_to_1mux_1_o_2[14]), .CLK(clk), .R(R), .O(SV[14]));
  flip_flop flip_flop_16 (.D(_16bit2_to_1mux_1_o_2[15]), .CLK(clk), .R(R), .O(SV[15]));
endmodule
