// Digital circuit XOR.dig as structural Verilog
module XOR (
  input  A,
  input  B,
  output O
);

  wire and_1_o, and_2_o, not_1_o, not_2_o;

  NOT not_1 (.A(A), .O(not_1_o));
  NOT not_2 (.A(B), .O(not_2_o));
  AND and_1 (.A(not_1_o), .B(B), .O(and_1_o));
  AND and_2 (.A(A), .B(not_2_o), .O(and_2_o));
  OR or_1 (.A(and_1_o), .B(and_2_o), .O(O));
endmodule
