// Digital circuit branch.dig as structural Verilog
module branch (
  input  [1:0] Cond,
  input  Zf,
  input  Nf,
  input  Vf,
  input  Branch,
  output JumpEn
);

  wire _4_to_1_mux_1_o, and_1_o, not_1_o, not_2_o, xor_1_o;

  NOT not_1 (.A(Zf), .O(not_1_o));
  XOR xor_1 (.A(Nf), .B(Vf), .O(xor_1_o));
  NOT not_2 (.A(xor_1_o), .O(not_2_o));
  AND and_1 (.A(not_1_o), .B(not_2_o), .O(and_1_o));
  _4_to_1_MUX _4_to_1_mux_1 (
    .S1(Cond[0]), .S2(Cond[1]), .A1(1'b1), .B1(Zf), .A2(not_1_o), .B2(and_1_o), .O(_4_to_1_mux_1_o));
  AND and_2 (.A(_4_to_1_mux_1_o), .B(Branch), .O(JumpEn));
endmodule
