// Digital circuit control.dig as structural Verilog
module control (
  input  [3:0] OP,
  output [12:0] OUT
);

  wire [14:0] _4_to_16_decoder_1_out;

  _4_to_16_decoder _4_to_16_decoder_1 (
    .sel(OP), .W(1'b1),
    .OUT({OUT[12], _4_to_16_decoder_1_out[14:9], OUT[7], _4_to_16_decoder_1_out[7:3], OUT[4], _4_to_16_decoder_1_out[1:0]}));
  or or_1 (OUT[0], _4_to_16_decoder_1_out[1], OUT[4], _4_to_16_decoder_1_out[3], _4_to_16_decoder_1_out[4], _4_to_16_decoder_1_out[5], _4_to_16_decoder_1_out[6], _4_to_16_decoder_1_out[7], _4_to_16_decoder_1_out[9], _4_to_16_decoder_1_out[10]);
  or or_2 (OUT[1], _4_to_16_decoder_1_out[1], OUT[4], _4_to_16_decoder_1_out[4], _4_to_16_decoder_1_out[6]);
  or or_3 (OUT[2], _4_to_16_decoder_1_out[3], _4_to_16_decoder_1_out[4]);
  or or_4 (OUT[3], _4_to_16_decoder_1_out[5], _4_to_16_decoder_1_out[6]);
  or or_5 (OUT[5], _4_to_16_decoder_1_out[7], _4_to_16_decoder_1_out[9]);
  or or_6 (OUT[6], _4_to_16_decoder_1_out[9], _4_to_16_decoder_1_out[10]);
  or or_7 (OUT[8], _4_to_16_decoder_1_out[11], _4_to_16_decoder_1_out[12], _4_to_16_decoder_1_out[13], _4_to_16_decoder_1_out[14]);
  or or_8 (OUT[9], _4_to_16_decoder_1_out[12], _4_to_16_decoder_1_out[14]);
  or or_9 (OUT[10], _4_to_16_decoder_1_out[13], _4_to_16_decoder_1_out[14]);
  or or_10 (OUT[11], _4_to_16_decoder_1_out[1], OUT[4]);
endmodule
