// Digital circuit flags.dig as structural Verilog
module flags (
  input  N,
  input  C,
  input  V,
  input  Z,
  input  FlagWrite,
  input  CLK,
  output Zf,
  output Nf,
  output Cf,
  output Vf
);

  Register register_1 (.D(Z), .C(CLK), .en(FlagWrite), .Q(Zf));
  Register register_2 (.D(N), .C(CLK), .en(FlagWrite), .Q(Nf));
  Register register_3 (.D(C), .C(CLK), .en(FlagWrite), .Q(Cf));
  Register register_4 (.D(V), .C(CLK), .en(FlagWrite), .Q(Vf));
endmodule
