// Digital circuit flip-flop.dig as structural Verilog
module flip_flop (
  input  D,
  input  CLK,
  input  R,
  output O
);

  wire d_latch_1_o, not_1_o;

  D_latch d_latch_1 (.D(D), .CLK(CLK), .R(R), .O(d_latch_1_o));
  NOT not_1 (.A(CLK), .O(not_1_o));
  D_latch d_latch_2 (.D(d_latch_1_o), .CLK(not_1_o), .R(R), .O(O));
endmodule
