// Digital circuit halfAdder.dig as structural Verilog
module halfAdder (
  input  A,
  input  B,
  output O,
  output C
);

  XOR xor_1 (.A(A), .B(B), .O(O));
  AND and_1 (.A(A), .B(B), .O(C));
endmodule
