// Digital circuit immediate.dig as structural Verilog
module immediate (
  input  [3:0] RA,
  input  [3:0] RB,
  input  [15:0] RDval,
  output [15:0] IMM,
  output [15:0] LUI
);


  assign IMM = {{8{1'b0}}, RA, RB};
  assign LUI = {RA, RB, RDval[7:0]};
endmodule
