// Digital circuit memory.dig as structural Verilog
module memory (
  input  [15:0] VALUE,
  input  clk,
  input  W,
  input  R,
  input  [3:0] RA,
  input  [3:0] RB,
  input  [3:0] RD,
  output [15:0] A,
  output [15:0] B
);

  wire [15:0] _4_to_16_decoder_1_out, register_1_sv, register_2_sv, register_3_sv, register_4_sv,
       register_5_sv, register_6_sv, register_7_sv, register_8_sv, register_9_sv, register_10_sv,
       register_11_sv, register_12_sv, register_13_sv, register_14_sv, register_15_sv, register_16_sv;

  _4_to_16_decoder _4_to_16_decoder_1 (.sel(RD), .W(W), .OUT(_4_to_16_decoder_1_out));
  Register register_1 (.Value(VALUE), .clk(clk), .WE(_4_to_16_decoder_1_out[0]), .R(R), .SV(register_1_sv));
  Register register_2 (.Value(VALUE), .clk(clk), .WE(_4_to_16_decoder_1_out[1]), .R(R), .SV(register_2_sv));
  Register register_3 (.Value(VALUE), .clk(clk), .WE(_4_to_16_decoder_1_out[2]), .R(R), .SV(register_3_sv));
  Register register_4 (.Value(VALUE), .clk(clk), .WE(_4_to_16_decoder_1_out[3]), .R(R), .SV(register_4_sv));
  Register register_5 (.Value(VALUE), .clk(clk), .WE(_4_to_16_decoder_1_out[4]), .R(R), .SV(register_5_sv));
  Register register_6 (.Value(VALUE), .clk(clk), .WE(_4_to_16_decoder_1_out[5]), .R(R), .SV(register_6_sv));
  Register register_7 (.Value(VALUE), .clk(clk), .WE(_4_to_16_decoder_1_out[6]), .R(R), .SV(register_7_sv));
  Register register_8 (.Value(VALUE), .clk(clk), .WE(_4_to_16_decoder_1_out[7]), .R(R), .SV(register_8_sv));
  Register register_9 (.Value(VALUE), .clk(clk), .WE(_4_to_16_decoder_1_out[8]), .R(R), .SV(register_9_sv));
  Register register_10 (.Value(VALUE), .clk(clk), .WE(_4_to_16_decoder_1_out[9]), .R(R), .SV(register_10_sv));
  Register register_11 (.Value(VALUE), .clk(clk), .WE(_4_to_16_decoder_1_out[10]), .R(R), .SV(register_11_sv));
  Register register_12 (.Value(VALUE), .clk(clk), .WE(_4_to_16_decoder_1_out[11]), .R(R), .SV(register_12_sv));
  Register register_13 (.Value(VALUE), .clk(clk), .WE(_4_to_16_decoder_1_out[12]), .R(R), .SV(register_13_sv));
  Register register_14 (.Value(VALUE), .clk(clk), .WE(_4_to_16_decoder_1_out[13]), .R(R), .SV(register_14_sv));
  Register register_15 (.Value(VALUE), .clk(clk), .WE(_4_to_16_decoder_1_out[14]), .R(R), .SV(register_15_sv));
  Register register_16 (.Value(VALUE), .clk(clk), .WE(_4_to_16_decoder_1_out[15]), .R(R), .SV(register_16_sv));
  _16bit_16_to_1_MUX MUXB (
    .D0(register_1_sv), .D1(register_2_sv), .D2(register_3_sv), .D3(register_4_sv), .D4(register_5_sv),
    .D5(register_6_sv), .D6(register_7_sv), .D7(register_8_sv), .D8(register_9_sv), .D9(register_10_sv),
    .D10(register_11_sv), .D11(register_12_sv), .D12(register_13_sv), .D13(register_14_sv),
    .D14(register_15_sv), .D15(register_16_sv), .S(RB), .Y(B));
  _16bit_16_to_1_MUX MUXA (
    .D0(register_1_sv), .D1(register_2_sv), .D2(register_3_sv), .D3(register_4_sv), .D4(register_5_sv),
    .D5(register_6_sv), .D6(register_7_sv), .D7(register_8_sv), .D8(register_9_sv), .D9(register_10_sv),
    .D10(register_11_sv), .D11(register_12_sv), .D12(register_13_sv), .D13(register_14_sv),
    .D14(register_15_sv), .D15(register_16_sv), .S(RA), .Y(A));
endmodule
