// Digital circuit memory8.dig as structural Verilog
module memory8 (
  input  clk,
  input  [15:0] value,
  input  [2:0] OPW,
  input  W,
  input  R,
  input  [2:0] RA,
  input  [2:0] RB,
  output [15:0] A,
  output [15:0] B
);

  wire [7:0] _3_to_8_decoder_1__000;
  wire [15:0] register_1_sv, register_2_sv, register_3_sv, register_4_sv, register_5_sv, register_6_sv,
       register_7_sv, register_8_sv;

  _3_to_8_decoder _3_to_8_decoder_1 (
    .chs(OPW), .W(W), ._000(_3_to_8_decoder_1__000[0]), ._001(_3_to_8_decoder_1__000[1]),
    ._010(_3_to_8_decoder_1__000[2]), ._011(_3_to_8_decoder_1__000[3]), ._100(_3_to_8_decoder_1__000[4]),
    ._101(_3_to_8_decoder_1__000[5]), ._110(_3_to_8_decoder_1__000[6]), ._111(_3_to_8_decoder_1__000[7]));
  Register register_1 (.Value(value), .clk(clk), .WE(_3_to_8_decoder_1__000[0]), .R(R), .SV(register_1_sv));
  Register register_2 (.Value(value), .clk(clk), .WE(_3_to_8_decoder_1__000[1]), .R(R), .SV(register_2_sv));
  Register register_3 (.Value(value), .clk(clk), .WE(_3_to_8_decoder_1__000[2]), .R(R), .SV(register_3_sv));
  Register register_4 (.Value(value), .clk(clk), .WE(_3_to_8_decoder_1__000[3]), .R(R), .SV(register_4_sv));
  Register register_5 (.Value(value), .clk(clk), .WE(_3_to_8_decoder_1__000[4]), .R(R), .SV(register_5_sv));
  Register register_6 (.Value(value), .clk(clk), .WE(_3_to_8_decoder_1__000[5]), .R(R), .SV(register_6_sv));
  Register register_7 (.Value(value), .clk(clk), .WE(_3_to_8_decoder_1__000[6]), .R(R), .SV(register_7_sv));
  Register register_8 (.Value(value), .clk(clk), .WE(_3_to_8_decoder_1__000[7]), .R(R), .SV(register_8_sv));
  _16bit_8_to_1_MUX _16bit_8_to_1_mux_1 (
    .OP(RA), .AD(register_1_sv), .SB(register_2_sv), .ND(register_3_sv), .OR(register_4_sv),
    .XR(register_5_sv), .NT(register_6_sv), .SP(register_7_sv), .SP2(register_8_sv), .OT(A));
  _16bit_8_to_1_MUX _16bit_8_to_1_mux_2 (
    .OP(RB), .AD(register_1_sv), .SB(register_2_sv), .ND(register_3_sv), .OR(register_4_sv),
    .XR(register_5_sv), .NT(register_6_sv), .SP(register_7_sv), .SP2(register_8_sv), .OT(B));
endmodule
