// Digital circuit writeback.dig as structural Verilog
module writeback (
  input  [15:0] ALU,
  input  [15:0] MEM,
  input  [15:0] IMM,
  input  [15:0] LUI,
  input  [1:0] WBsrc,
  output [15:0] WBdata
);

  wire [15:0] MUXA_o, MUXB_o;

  _16bit2_to_1MUX MUXA (.A(ALU), .B(MEM), .S(WBsrc[0]), .O(MUXA_o));
  _16bit2_to_1MUX MUXB (.A(IMM), .B(LUI), .S(WBsrc[0]), .O(MUXB_o));
  _16bit2_to_1MUX MUXF (.A(MUXA_o), .B(MUXB_o), .S(WBsrc[1]), .O(WBdata));
endmodule
